# Fritzing sketch lesson_2 (saved by Fritzing 0.9.3b)
breadboards: 2

parts:
  U1 = ESP-32 Wide FINAL [part_number="DOIT ESP-32"]
  Part1 = GY-BMEP280 Barometric Pressure Sensor - Breakout
  ZS-042_RTC1 = ZS-042 RTC Module

nets:
  N1: U1.3.3, Part1.SDA, ZS-042_RTC1.VCC
  GND: U1.GND, Part1.SCL, ZS-042_RTC1.GND
  N2: U1.GPIO21, Part1.VCC, ZS-042_RTC1.SDA
  N3: U1.GPIO22, Part1.GND, ZS-042_RTC1.SCL

custom parts:
  ESP-32 Wide FINAL: DOIT ESP-32 30 Pin
  GY-BMEP280 Barometric Pressure Sensor - Breakout: The BME280 is a chip which was originally designed for the next generation of smartphones. It is made up of a very accurate pressure sensor and an associated temperature sensor which helps calibrate the pressure readings. And just for fun they threw in a pretty solid humidity sensor in there as well! So with an I2C connection you have access to enough weather data to make some pretty good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
